# Fritzing sketch light_sensor (saved by Fritzing 0.9.0b)
circuit board: 8.46667cm x 5.64444cm
breadboards: 1

parts:
  Part1 = Arduino Uno (Rev3)
  SENSOR1 = TCS34725 RGB Color Sensor
  R1 = Resistor [tolerance=±5% resistance=680 package=THT]
  R2 = Resistor [tolerance=±5% resistance=1k package=THT]
  R3 = Resistor [tolerance=±5% resistance=680 package=THT]
  LED1 = RGB LED - (4 legs) [package="5 mm [THT]"]

nets:
  N1: Part1.A4/SDA, SENSOR1.SDA
  N2: Part1.A5/SCL, SENSOR1.SCL
  GND: Part1.GND, SENSOR1.GND
  N3: Part1.D3_PWM, R2.Pin_0
  N4: Part1.D5_PWM, R3.Pin_0
  N5: Part1.D6_PWM, R1.Pin_0
  5V: Part1.5V, SENSOR1.VDD, LED1.common_anode
  N6: R1.Pin_1, LED1.blue_cathode
  N7: R2.Pin_1, LED1.red_cathode
  N8: R3.Pin_1, LED1.green_cathode

custom parts:
  TCS34725 RGB Color Sensor: TCS34725 RGB Color Sensor with LED
